# Fritzing sketch TimeDog-Proto-v0 (saved by Fritzing 0.7.12b)
breadboards: 1

parts:
  U1 = atmega328 [package=dip]
  XTAL1 = Crystal [package=THT]
  C1 = Ceramic Disk Capacitor [package=THT]
  C2 = Ceramic Disk Capacitor [package=THT]
  J5 = Generic female header - metal rounded - 7 pins [package=THT]
  J7 = Generic female header [package=THT]  # not connected
  J8 = Piezo Speaker
  R1 = Resistor [tolerance=±5% resistance=220 package=THT]
  Q1 = NPN-Transistor [package="SOT-23 [SMD]"]
  J9 = Generic female header - 4 pins [package=THT]
  J10 = Generic female header - 4 pins [package=THT]
  K1 = Relay [part_number=FRS1B-S package=THT]
  J11 = female pin header, 2 pins [form="♀ (female)"]

nets:
  N1: U1.RESET, J5.pin4
  N2: U1.D0_(RX), J5.pin5
  N3: U1.D1_(TX), J5.pin6
  N4: U1.D2, J9.pin4
  N5: U1.D3_(PWM), J9.pin3
  N6: U1.D4, Q1.0
  N7: U1.VCC, J9.pin1
  N8: U1.GND#7, C1.pin_1, C2.pin_0, J8.pin1, Q1.1, K1.B
  N9: U1.XLAT1, XTAL1.pin_0, C2.pin_1
  N10: U1.XLAT2, XTAL1.pin_1
  N11: U1.D7, R1.Pin_1
  N12: U1.D10_(PWM), K1.A
  N13: U1.D11_(PWM), J5.pin3
  N14: U1.D12, J5.pin2
  N15: U1.D13, J5.pin1
  N16: U1.AVCC, J10.pin1, J10.pin2
  N17: U1.A4, J10.pin3
  N18: U1.A5, J10.pin4
  N19: J8.pin2, R1.Pin_0
  N20: Q1.2, J9.pin2
  N21: K1.COIL2, J11.pin2
